// Logisim project CPU1-RCAGAMEZ.circ as structural Verilog: 9 circuits, main circuit main
module main (
);

  wire ALUSRC, CLK, debugcomponent_1_aand, debugcomponent_1_add, debugcomponent_1_addi, debugcomponent_1_beq,
       debugcomponent_1_bnq, debugcomponent_1_jump, debugcomponent_1_load, debugcomponent_1_none,
       debugcomponent_1_oor, debugcomponent_1_store, debugcomponent_1_sub, REGDST, REGWRITE, Rst, uc_1_beq,
       uc_1_bne, uc_1_jump, uc_1_memread, uc_1_memtoreg, uc_1_memwrite;
  wire [1:0] uc_1_alu, ucalu_1_output;
  wire [4:0] id_1_shamt, multiplexer_1_out, RD, RS, RT;
  wire [5:0] FUNC, OPCODE;
  wire [15:0] IMM;
  wire [23:0] adder_1_out, Iter;
  wire [25:0] id_1_jumadd;
  wire [31:0] adder_2_out, bit_extender_1_out, multiplexer_2_out, ram_1_dout, ur_1_ra, ur_1_rb;

  RAM #(.addrWidth(24), .dataWidth(32), .enables("line")) ram_1 (.addr(Iter), .dout(ram_1_dout));  // open: we, clk, din
  Button button_1 (.out(Rst));
  Clock clock_1 (.out(CLK));
  Register #(.width(24)) register_1 (.D(adder_1_out), .Q(Iter), .clk(CLK), .clr(Rst));  // open: en
  Adder #(.width(24)) adder_1 (.a(Iter), .b(24'h1), .out(adder_1_out));  // open: cin, cout
  Multiplexer #(.width(5)) multiplexer_1 (.in0(RT), .in1(RD), .out(multiplexer_1_out), .sel(REGDST));
  // Probe on debugcomponent_1_addi
  DebugComponent debugcomponent_1 (
    .opCode(OPCODE), .funct(FUNC), .Addi(debugcomponent_1_addi), .Load(debugcomponent_1_load),
    .Store(debugcomponent_1_store), .BEQ(debugcomponent_1_beq), .BNQ(debugcomponent_1_bnq),
    .Jump(debugcomponent_1_jump), .None(debugcomponent_1_none), .Add(debugcomponent_1_add),
    .Sub(debugcomponent_1_sub), .AAnd(debugcomponent_1_aand), .OOr(debugcomponent_1_oor));
  // Probe on debugcomponent_1_load
  // Probe on debugcomponent_1_store
  // Probe on debugcomponent_1_beq
  // Probe on debugcomponent_1_bnq
  // Probe on debugcomponent_1_jump
  // Probe on debugcomponent_1_none
  // Probe on debugcomponent_1_add
  // Probe on debugcomponent_1_sub
  // Probe on debugcomponent_1_aand
  // Probe on debugcomponent_1_oor
  ID id_1 (
    .INPUTID(ram_1_dout), .Funct(FUNC), .Shamt(id_1_shamt), .Inmediate(IMM), .RD(RD), .RT(RT), .RS(RS),
    .OPCODE(OPCODE), .JumAdd(id_1_jumadd));
  // Probe on FUNC
  // Probe on id_1_shamt
  // Probe on id_1_jumadd
  UR ur_1 (
    .BUSW(adder_2_out), .RESET(Rst), .RS(RS), .CLK(CLK), .RT(RT), .RW(multiplexer_1_out),
    .REGWRITE(REGWRITE), .RA(ur_1_ra), .RB(ur_1_rb));
  assign bit_extender_1_out = {{16{IMM[15]}}, IMM};  // Bit_Extender bit_extender_1
  UC uc_1 (
    .opcode(OPCODE), .regdst(REGDST), .regwrite(REGWRITE), .jump(uc_1_jump), .beq(uc_1_beq), .bne(uc_1_bne),
    .alusrc(ALUSRC), .memToReg(uc_1_memtoreg), .memRead(uc_1_memread), .memWrite(uc_1_memwrite),
    .ALU(uc_1_alu));
  // Probe on uc_1_jump
  // Probe on uc_1_beq
  // Probe on uc_1_bne
  // Probe on uc_1_memtoreg
  // Probe on uc_1_memread
  // Probe on uc_1_memwrite
  // Probe on uc_1_alu
  Multiplexer #(.width(32)) multiplexer_2 (
    .in0(ur_1_rb), .in1(bit_extender_1_out), .out(multiplexer_2_out), .sel(ALUSRC));
  Adder #(.width(32)) adder_2 (.a(ur_1_ra), .b(multiplexer_2_out), .out(adder_2_out));  // open: cin, cout
  // Probe on ucalu_1_output
  UCALU ucalu_1 (.ALUOP(uc_1_alu), .FUNC(FUNC), .OUTPUT(ucalu_1_output));
  // Probe on adder_2_out
endmodule

module ID (
  input  [31:0] INPUTID,
  output [5:0] Funct,
  output [4:0] Shamt,
  output [15:0] Inmediate,
  output [4:0] RD,
  output [4:0] RT,
  output [4:0] RS,
  output [5:0] OPCODE,
  output [25:0] JumAdd
);

  wire J, not_1_out, or_1_out, R;

  Comparator #(.width(6)) comparator_1 (.a(INPUTID[31:26]), .b(6'b000010), .eq(J));  // open: gt, lt
  Multiplexer #(.width(26)) multiplexer_1 (.in1(INPUTID[25:0]), .out(JumAdd), .sel(J));  // open: in0
  or or_1 (or_1_out, R, J);
  Multiplexer #(.width(16)) multiplexer_2 (.in1(INPUTID[15:0]), .out(Inmediate), .sel(not_1_out));  // open: in0
  not not_1 (not_1_out, or_1_out);
  Comparator #(.width(6)) comparator_2 (.a(INPUTID[31:26]), .b({6{1'b0}}), .eq(R));  // open: gt, lt
  Multiplexer #(.width(16)) multiplexer_3 (.in1(INPUTID[15:0]), .out({RD, Shamt, Funct}), .sel(R));  // open: in0

  assign OPCODE = INPUTID[31:26];
  assign RS = INPUTID[25:21];
  assign RT = INPUTID[20:16];

  // Other names for the same wires on the sheet: OP[5:0] = INPUTID[31:26]; JUMP[25:0] = JumAdd

  // Notes on the sheet:
  //   Cuando es J
  //   Cuando es R
endmodule

module UC (
  input  [5:0] opcode,
  output regdst,
  output regwrite,
  output jump,
  output beq,
  output bne,
  output alusrc,
  output memToReg,
  output memRead,
  output memWrite,
  output [1:0] ALU
);

  wire and_2_out, and_3_out, not_1_out, not_2_out, not_3_out, not_4_out;

  not not_1 (not_1_out, opcode[3]);
  not not_2 (not_2_out, opcode[2]);
  not not_3 (not_3_out, opcode[1]);
  not not_4 (not_4_out, opcode[0]);
  and and_1 (regdst, not_1_out, not_2_out, not_3_out);
  and and_2 (and_2_out, not_2_out, not_3_out);
  and and_3 (and_3_out, opcode[5], not_1_out);
  and and_4 (jump, opcode[1], not_4_out);
  and and_5 (beq, not_3_out, opcode[0]);
  and and_6 (bne, opcode[2], not_4_out);
  or or_1 (alusrc, opcode[3], opcode[5]);
  and and_7 (memToReg, opcode[5], not_1_out);
  and and_8 (memRead, opcode[5], not_1_out);
  and and_9 (memWrite, opcode[3], opcode[1]);
  and and_10 (ALU[1], not_1_out, not_2_out, not_3_out);
  or or_2 (regwrite, and_2_out, and_3_out);

  assign ALU[0] = opcode[2];
endmodule

module DebugComponent (
  input  [5:0] opCode,
  input  [5:0] funct,
  output Addi,
  output Load,
  output Store,
  output BEQ,
  output BNQ,
  output Jump,
  output None,
  output Add,
  output Sub,
  output AAnd,
  output OOr
);

  wire nonoOrR;

  debugStep1 debugstep1_1 (
    .opcode(opCode), .noneOrR(nonoOrR), .addi(Addi), .load(Load), .store(Store), .beq(BEQ), .bnq(BNQ),
    .jump(Jump));
  debugStep2 debugstep2_1 (.noneOrR(nonoOrR), .funct(funct), .none(None), .add(Add), .sub(Sub), .aand(AAnd), .oor(OOr));
endmodule

module debugStep1 (
  input  [5:0] opcode,
  output noneOrR,
  output addi,
  output load,
  output store,
  output beq,
  output bnq,
  output jump
);

  wire not_1_out, not_2_out, not_3_out, not_4_out, not_5_out, not_6_out;

  not not_1 (not_1_out, opcode[5]);
  not not_2 (not_2_out, opcode[4]);
  not not_3 (not_3_out, opcode[3]);
  not not_4 (not_4_out, opcode[2]);
  not not_5 (not_5_out, opcode[1]);
  not not_6 (not_6_out, opcode[0]);
  and and_1 (noneOrR, not_1_out, not_2_out, not_3_out, not_4_out, not_5_out, not_6_out);
  and and_2 (addi, not_1_out, not_2_out, opcode[3], not_4_out, not_5_out, not_6_out);
  and and_3 (load, opcode[5], not_2_out, not_3_out, not_4_out, opcode[1], opcode[0]);
  and and_4 (store, opcode[5], not_2_out, opcode[3], not_4_out, opcode[1], opcode[0]);
  and and_5 (beq, not_1_out, not_2_out, not_3_out, opcode[2], not_5_out, not_6_out);
  and and_6 (bnq, not_1_out, not_2_out, not_3_out, opcode[2], not_5_out, opcode[0]);
  and and_7 (jump, not_1_out, not_2_out, not_3_out, not_4_out, opcode[1], not_6_out);
endmodule

module debugStep2 (
  input  noneOrR,
  input  [5:0] funct,
  output none,
  output add,
  output sub,
  output aand,
  output oor
);

  wire not_1_out, not_2_out, not_3_out, not_4_out, not_5_out, not_6_out;

  not not_1 (not_1_out, funct[5]);
  not not_2 (not_2_out, funct[4]);
  not not_3 (not_3_out, funct[3]);
  not not_4 (not_4_out, funct[2]);
  not not_5 (not_5_out, funct[1]);
  not not_6 (not_6_out, funct[0]);
  and and_1 (none, noneOrR, not_1_out, not_2_out, not_3_out, not_4_out, not_5_out, not_6_out);
  and and_2 (add, noneOrR, funct[5], not_2_out, not_3_out, not_4_out, not_5_out, not_6_out);
  and and_3 (sub, noneOrR, funct[5], not_2_out, not_3_out, not_4_out, funct[1], not_6_out);
  and and_4 (aand, noneOrR, funct[5], not_2_out, not_3_out, funct[2], not_5_out, not_6_out);
  and and_5 (oor, noneOrR, funct[5], not_2_out, not_3_out, funct[2], not_5_out, funct[0]);
endmodule

module UCALU (
  input  [1:0] ALUOP,
  input  [5:0] FUNC,
  output [1:0] OUTPUT
);

  wire and_1_out, and_2_out, and_3_out, and_4_out, not_1_out, not_2_out, not_3_out, not_4_out, not_5_out,
       not_6_out, not_7_out;

  not not_1 (not_1_out, ALUOP[1]);
  not not_2 (not_2_out, ALUOP[0]);
  not not_3 (not_3_out, FUNC[4]);
  not not_4 (not_4_out, FUNC[3]);
  not not_5 (not_5_out, FUNC[2]);
  not not_6 (not_6_out, FUNC[1]);
  not not_7 (not_7_out, FUNC[0]);
  or or_1 (OUTPUT[1], not_1_out, and_1_out);
  and and_1 (and_1_out, not_2_out, FUNC[5], not_3_out, not_4_out, not_5_out, not_7_out);
  and and_2 (and_2_out, ALUOP[1], not_2_out, FUNC[5], not_3_out, not_4_out, not_5_out, FUNC[1], not_7_out);
  and and_3 (and_3_out, ALUOP[1], not_2_out, FUNC[5], not_3_out, not_4_out, FUNC[2], not_6_out, FUNC[0]);
  or or_2 (OUTPUT[0], and_2_out, and_3_out, and_4_out);
  and and_4 (and_4_out, not_1_out, ALUOP[0]);
endmodule

module UR (
  input  [31:0] BUSW,
  input  RESET,
  input  [4:0] RS,
  input  CLK,
  input  [4:0] RT,
  input  [4:0] RW,
  input  REGWRITE,
  output [31:0] RA,
  output [31:0] RB
);

  wire EnaT0, EnaT1, EnaT2, EnaT3, EnaT4, EnaT5, EnaT6, EnaT7, EnaT8, EnaT9, EnaT10, EnaT11, EnaT12, EnaT13,
       EnaT14, EnaT15, EnaT16, EnaT17, EnaT18, EnaT19, EnaT20, EnaT21, EnaT22, EnaT23, EnaT24;
  wire [31:0] DT0, DT1, DT2, DT3, DT4, DT5, DT6, DT7, DT8, DT9, DT10, DT11, DT12, DT13, DT14, DT15, DT16,
       DT17, DT18, DT19, DT20, DT21, DT22, DT23, DT24, R8, R9, R10, R11, R12, R13, R14, R15, R16, R17, R18,
       R19, R20, R21, R22, R23, R24, R25, R26, R27, R28, R29, R30, R31, R32;

  Demultiplexer #(.select(5), .width(32)) demultiplexer_1 (
    .out7(DT0), .out8(DT1), .out9(DT2), .out10(DT3), .out11(DT4), .out12(DT5), .out13(DT6), .out14(DT7),
    .out15(DT8), .out16(DT9), .out17(DT10), .out18(DT11), .out19(DT12), .out20(DT13), .out21(DT14),
    .out22(DT15), .out23(DT16), .out24(DT17), .out25(DT18), .out26(DT19), .out27(DT20), .out28(DT21),
    .out29(DT22), .out30(DT23), .out31(DT24), .in(BUSW), .sel(RW));  // open: out0, out1, out2, out3, out4, out5, out6
  Demultiplexer #(.select(5)) demultiplexer_2 (
    .out7(EnaT0), .out8(EnaT1), .out9(EnaT2), .out10(EnaT3), .out11(EnaT4), .out12(EnaT5), .out13(EnaT6),
    .out14(EnaT7), .out15(EnaT8), .out16(EnaT9), .out17(EnaT10), .out18(EnaT11), .out19(EnaT12),
    .out20(EnaT13), .out21(EnaT14), .out22(EnaT15), .out23(EnaT16), .out24(EnaT17), .out25(EnaT18),
    .out26(EnaT19), .out27(EnaT20), .out28(EnaT21), .out29(EnaT22), .out30(EnaT23), .out31(EnaT24),
    .in(REGWRITE), .sel(RW));  // open: out0, out1, out2, out3, out4, out5, out6
  Register #(.width(32)) t0 (.D(DT0), .en(EnaT0), .Q(R8), .clk(CLK), .clr(RESET));
  Register #(.width(32)) t1 (.D(DT1), .en(EnaT1), .Q(R9), .clk(CLK), .clr(RESET));
  Register #(.width(32)) t2 (.D(DT2), .en(EnaT2), .Q(R10), .clk(CLK), .clr(RESET));
  Register #(.width(32)) t3 (.D(DT3), .en(EnaT3), .Q(R11), .clk(CLK), .clr(RESET));
  Register #(.width(32)) t4 (.D(DT4), .en(EnaT4), .Q(R12), .clk(CLK), .clr(RESET));
  Register #(.width(32)) t5 (.D(DT5), .en(EnaT5), .Q(R13), .clk(CLK), .clr(RESET));
  Register #(.width(32)) t6 (.D(DT6), .en(EnaT6), .Q(R14), .clk(CLK), .clr(RESET));
  Register #(.width(32)) t7 (.D(DT7), .en(EnaT7), .Q(R15), .clk(CLK), .clr(RESET));
  Register #(.width(32)) t8 (.D(DT8), .en(EnaT8), .Q(R16), .clk(CLK), .clr(RESET));
  Register #(.width(32)) t9 (.D(DT9), .en(EnaT9), .Q(R17), .clk(CLK), .clr(RESET));
  Register #(.width(32)) t10 (.D(DT10), .en(EnaT10), .Q(R18), .clk(CLK), .clr(RESET));
  Register #(.width(32)) t11 (.D(DT11), .en(EnaT11), .Q(R19), .clk(CLK), .clr(RESET));
  Register #(.width(32)) t12 (.D(DT12), .en(EnaT12), .Q(R20), .clk(CLK), .clr(RESET));
  Register #(.width(32)) t13 (.D(DT13), .en(EnaT13), .Q(R21), .clk(CLK), .clr(RESET));
  Register #(.width(32)) t14 (.D(DT14), .en(EnaT14), .Q(R22), .clk(CLK), .clr(RESET));
  Register #(.width(32)) t15 (.D(DT15), .en(EnaT15), .Q(R23), .clk(CLK), .clr(RESET));
  Register #(.width(32)) t16 (.D(DT16), .en(EnaT16), .Q(R24), .clk(CLK), .clr(RESET));
  Register #(.width(32)) t17 (.D(DT17), .en(EnaT17), .Q(R25), .clk(CLK), .clr(RESET));
  Register #(.width(32)) t18 (.D(DT18), .en(EnaT18), .Q(R25), .clk(CLK), .clr(RESET));
  Register #(.width(32)) t19 (.D(DT19), .en(EnaT19), .Q(R26), .clk(CLK), .clr(RESET));
  Register #(.width(32)) t20 (.D(DT20), .en(EnaT20), .Q(R27), .clk(CLK), .clr(RESET));
  Register #(.width(32)) t21 (.D(DT21), .en(EnaT21), .Q(R28), .clk(CLK), .clr(RESET));
  Register #(.width(32)) t22 (.D(DT22), .en(EnaT22), .Q(R28), .clk(CLK), .clr(RESET));
  Register #(.width(32)) t23 (.D(DT23), .en(EnaT23), .Q(R28), .clk(CLK), .clr(RESET));
  Register #(.width(32)) t24 (.D(DT24), .en(EnaT24), .Q(R29), .clk(CLK), .clr(RESET));
  Multiplexer #(.select(5), .width(32)) multiplexer_1 (
    .in7(R8), .in8(R9), .in9(R10), .in10(R11), .in11(R12), .in12(R13), .in13(R14), .in14(R15), .in15(R16),
    .in16(R17), .in17(R18), .in18(R19), .in19(R20), .in20(R21), .in21(R22), .in22(R23), .in23(R24),
    .in24(R25), .in25(R26), .in26(R27), .in27(R28), .in28(R29), .in29(R30), .in30(R31), .in31(R32), .out(RA),
    .sel(RS));  // open: in0, in1, in2, in3, in4, in5, in6
  Multiplexer #(.select(5), .width(32)) multiplexer_2 (
    .in7(R8), .in8(R9), .in9(R10), .in10(R11), .in11(R12), .in12(R13), .in13(R14), .in14(R15), .in15(R16),
    .in16(R17), .in17(R18), .in18(R19), .in19(R20), .in20(R21), .in21(R22), .in22(R23), .in23(R24),
    .in24(R25), .in25(R26), .in26(R27), .in27(R28), .in28(R29), .in29(R30), .in30(R31), .in31(R32), .out(RB),
    .sel(RT));  // open: in0, in1, in2, in3, in4, in5, in6

  // Other names for the same wires on the sheet: TSELECTORA[4:0] = RS; TSELECTORB[4:0] = RT; TSELECTORR[4:0] = RW
endmodule

module TSelector (
  input  [4:0] DIR,
  output [2:0] OUTPUT
);


  assign OUTPUT = DIR[2:0];
endmodule
